// Logisim project 4X1 MUX Basic Circuit.circ as structural Verilog: 1 circuit, main circuit main
module main (
  input  in_1,
  input  in_2,
  input  in_3,
  input  in_4,
  input  in_5,
  input  in_6,
  output out_7
);

  wire and_1_out, and_2_out, and_3_out, and_4_out, not_1_out, not_2_out;

  not not_1 (not_1_out, in_1);
  not not_2 (not_2_out, in_2);
  and and_1 (and_1_out, in_1, in_2, in_3);
  and and_2 (and_2_out, not_2_out, in_1, in_4);
  and and_3 (and_3_out, in_2, not_1_out, in_5);
  and and_4 (and_4_out, not_2_out, not_1_out, in_6);
  ExactlyOne xor_1 (.out(out_7), .in0(and_1_out), .in1(and_2_out), .in2(and_3_out), .in3(and_4_out));
endmodule
