// Logisim project Full Adder using  4X1 MUX.circ as structural Verilog: 1 circuit, main circuit main
module main (
  input  C,
  input  B,
  input  A,
  input  X,
  input  Y,
  output S,
  output CARRY
);

  wire not_1_out;

  not not_1 (not_1_out, C);
  // MUX_main main_1: pin names not known; wires that end beside it: B, A, C, not_1_out, not_1_out, C, S
  // MUX_main main_2: pin names not known; wires that end beside it: B, A, X, C, C, Y, CARRY

  // Notes on the sheet:
  //   C
  //   B
  //   A
endmodule
