// Logisim project Full Subtractor using 4X1 MUX.circ as structural Verilog: 1 circuit, main circuit main
module main (
  input  A,
  input  B,
  input  Bin,
  input  in_4,
  input  in_5,
  output out_6,
  output out_7
);

  wire not_1_out;

  not not_1 (not_1_out, Bin);
  // MUX_main main_1: pin names not known; wires that end beside it: A, B, Bin, not_1_out, not_1_out, Bin, out_6
  // MUX_main main_2: pin names not known; wires that end beside it: A, B, Bin, in_4, in_5, Bin, out_7
endmodule
