// Logisim project Half Adder using 4X1 MUX.circ as structural Verilog: 1 circuit, main circuit main
module main (
  input  in_1,
  input  in_2,
  input  [1:0] in_3,
  input  in_4,
  input  in_5,
  input  in_6,
  input  in_7,
  input  in_8,
  input  in_9,
  output out_10,
  output out_11
);

  Multiplexer #(.select(2), .enable("false")) multiplexer_1 (
    .in0(in_1), .in1(in_2), .in2(in_4), .in3(in_5), .out(out_10), .sel(in_3));
  Multiplexer #(.select(2), .enable("false")) multiplexer_2 (
    .in0(in_6), .in1(in_7), .in2(in_8), .in3(in_9), .out(out_11), .sel(in_3));
endmodule
