// Logisim project Half Subtractor using 4X1 MUX.circ as structural Verilog: 1 circuit, main circuit main
module main (
  input  in_1,
  input  in_2,
  input  A,
  input  B,
  input  in_5,
  input  in_6,
  output DIFFERENCE,
  output BORROW
);

  // MUX_main main_1: pin names not known; wires that end beside it: A, B, in_1, in_2, in_2, in_1, DIFFERENCE
  // MUX_main main_2: pin names not known; wires that end beside it: A, B, in_5, in_5, in_6, in_5, BORROW

  // Notes on the sheet:
  //   A
  //   B
  //   Diff
  //   Borrow
endmodule
