// Logisim project Parallel Adder.circ as structural Verilog: 1 circuit, main circuit main
module main (
  input  C,
  input  [3:0] A,
  input  [3:0] B,
  output [3:0] S,
  output Cout
);

  wire main_1_p5, main_2_p5, main_3_p5;

  // lab3_fullAdder_main main_1: pin names not known; wires that end beside it: C, A[0], B[0], S[0], main_1_p5
  // lab3_fullAdder_main main_2: pin names not known; wires that end beside it: main_1_p5, A[1], B[1], S[1], main_2_p5
  // lab3_fullAdder_main main_3: pin names not known; wires that end beside it: main_2_p5, A[2], B[2], S[2], main_3_p5
  // lab3_fullAdder_main main_4: pin names not known; wires that end beside it: main_3_p5, A[3], B[3], S[3], Cout
endmodule
